// Logisim project analyzer_7400.circ as structural Verilog: 6 circuits, main circuit main
module mem_16x8 (
  input  [7:0] Din,
  input  [3:0] ADDRin,
  input  [7:0] WORD,
  input  WORDen,
  input  CLK,
  input  RUN,
  input  HLT,
  output [7:0] Dout,
  output [3:0] MEM,
  output FIN
);

  wire and1_pin1, and4_pin8, and4_pin10, comparator1_pin3, comparator1_pin6, comparator2_pin3,
       comparator2_pin6, counter_pin1, counter_pin2, counter_pin7, counter_pin9, counter_pin10, dflip_pin1,
       dflip_pin2, dflip_pin3, dflip_pin4, dflip_pin5, dflip_pin9, dflip_pin10, dflip_pin13, mult2to1_pin2,
       mult2to1_pin5, mult2to1_pin11, mult2to1_pin14, mult2to1_pin15, not1_pin4, not1_pin6, not1_pin10,
       RAM1_no1, RAM1_no2, RAM1_no3, RAM1_no4, RAM2_no1, RAM2_no2, RAM2_no3, RAM2_no4;

  _7485 comparator1 (
    .pin1(WORD[7]), .pin3(comparator1_pin3), .pin6(comparator1_pin6), .pin15(Din[0]), .pin14(WORD[6]),
    .pin13(Din[1]), .pin12(Din[2]), .pin11(WORD[5]), .pin10(Din[3]), .pin9(WORD[4]));  // open: pin2, pin4, pin5, pin7
  _7485 comparator2 (
    .pin1(WORD[3]), .pin3(comparator2_pin3), .pin6(comparator2_pin6), .pin15(Din[4]), .pin14(WORD[2]),
    .pin13(Din[5]), .pin12(Din[6]), .pin11(WORD[1]), .pin10(Din[7]), .pin9(WORD[0]));  // open: pin2, pin4, pin5, pin7
  _7421 and4 (
    .pin13(comparator1_pin6), .pin12(comparator2_pin6), .pin10(and4_pin10), .pin9(WORDen), .pin8(and4_pin8));  // open: pin1, pin2, pin3, pin4, pin5, pin6, pin11
  _74157 mult2to1 (
    .pin1(FIN), .pin2(mult2to1_pin2), .pin3(ADDRin[0]), .pin4(MEM[0]), .pin5(mult2to1_pin5),
    .pin6(ADDRin[1]), .pin7(MEM[1]), .pin15(mult2to1_pin15), .pin14(mult2to1_pin14), .pin13(ADDRin[3]),
    .pin12(MEM[3]), .pin11(mult2to1_pin11), .pin10(ADDRin[2]), .pin9(MEM[2]));
  _74161 counter (
    .pin1(counter_pin1), .pin2(counter_pin2), .pin7(counter_pin7), .pin14(mult2to1_pin2),
    .pin13(mult2to1_pin5), .pin12(mult2to1_pin11), .pin11(mult2to1_pin14), .pin10(counter_pin10),
    .pin9(counter_pin9));  // open: pin3, pin4, pin5, pin6, pin15
  _7408 and1 (
    .pin1(and1_pin1), .pin2(CLK), .pin3(counter_pin2));  // open: pin4, pin5, pin6, pin13, pin12, pin11, pin10, pin9, pin8
  _7474 dflip (
    .pin1(dflip_pin1), .pin2(dflip_pin2), .pin3(dflip_pin3), .pin4(dflip_pin4), .pin5(dflip_pin5),
    .pin13(dflip_pin13), .pin12(and4_pin8), .pin11(CLK), .pin10(dflip_pin10), .pin9(dflip_pin9));  // open: pin6, pin8
  _7432 or1 (
    .pin1(RUN), .pin2(dflip_pin2), .pin3(dflip_pin3), .pin4(HLT), .pin5(dflip_pin9), .pin6(dflip_pin2));  // open: pin13, pin12, pin11, pin10, pin9, pin8
  SN74LS189 RAM1 (
    .nCS(1'b0), .nWE(not1_pin10), .A3(MEM[0]), .D4(Din[0]), .A2(MEM[1]), .D3(Din[1]), .A1(MEM[2]),
    .D2(Din[2]), .A0(MEM[3]), .D1(Din[3]), .nO4(RAM1_no4), .nO3(RAM1_no3), .nO2(RAM1_no2), .nO1(RAM1_no1));
  SN74LS189 RAM2 (
    .nCS(1'b0), .nWE(not1_pin10), .A3(MEM[0]), .D4(Din[4]), .A2(MEM[1]), .D3(Din[5]), .A1(MEM[2]),
    .D2(Din[6]), .A0(MEM[3]), .D1(Din[7]), .nO4(RAM2_no4), .nO3(RAM2_no3), .nO2(RAM2_no2), .nO1(RAM2_no1));
  SN74LS279 SR (.S4(not1_pin4), .R4(not1_pin6), .Q4(FIN));  // open: S1_2, R1, S2, R2, S3_1, S3_2, R3, S1_1, Q1, Q2, Q3
  _7404 nRAM1 (
    .pin3(RAM1_no1), .pin4(Dout[3]), .pin5(RAM1_no2), .pin6(Dout[2]), .pin11(RAM1_no3), .pin10(Dout[1]),
    .pin9(RAM1_no4), .pin8(Dout[0]));  // open: pin1, pin2, pin13, pin12
  _7404 nRAM2 (
    .pin3(RAM2_no1), .pin4(Dout[7]), .pin5(RAM2_no2), .pin6(Dout[6]), .pin11(RAM2_no3), .pin10(Dout[5]),
    .pin9(RAM2_no4), .pin8(Dout[4]));  // open: pin1, pin2, pin13, pin12
  _7404 not1 (
    .pin1(FIN), .pin2(and1_pin1), .pin3(dflip_pin5), .pin4(not1_pin4), .pin5(RUN), .pin6(not1_pin6),
    .pin13(dflip_pin2), .pin12(counter_pin9), .pin11(counter_pin2), .pin10(not1_pin10));  // open: pin9, pin8
  // also tied to GND on the sheet: mult2to1_pin15
  // also tied to VCC on the sheet: {and4_pin10, comparator1_pin3, comparator2_pin3, counter_pin1, dflip_pin1, dflip_pin13, dflip_pin4, dflip_pin10, counter_pin10, counter_pin7}
endmodule

module SN74LS189 (
  input  A3,
  input  A2,
  input  A1,
  input  A0,
  input  nCS,
  input  nWE,
  input  D4,
  input  D3,
  input  D2,
  input  D1,
  output nO4,
  output nO3,
  output nO2,
  output nO1
);

  wire nor_1_out;
  wire [3:0] ram_1_dout;

  nor nor_1 (nor_1_out, nCS, nWE);
  RAM #(.addrWidth(4), .dataWidth(4), .enables("line"), .trigger("high")) ram_1 (
    .addr({A3, A2, A1, A0}), .we(nor_1_out), .clk(1'b1), .din({D4, D3, D2, D1}), .dout(ram_1_dout));
  not not_1 (nO4, ram_1_dout[3]);
  not not_2 (nO3, ram_1_dout[2]);
  not not_3 (nO2, ram_1_dout[1]);
  not not_4 (nO1, ram_1_dout[0]);
endmodule

module SN74LS279 (
  input  S1_1,
  input  S1_2,
  input  R1,
  input  S2,
  input  R2,
  input  S3_1,
  input  S3_2,
  input  R3,
  input  S4,
  input  R4,
  output Q1,
  output Q2,
  output Q3,
  output Q4
);

  wire nor_1_out, nor_2_out, not_1_out, not_2_out, not_3_out, not_4_out, not_5_out, not_6_out;

  S_R_Flip_Flop #(.trigger("low")) s_r_ff_1 (
    .S(nor_1_out), .R(not_1_out), .clk(1'b0), .Q(Q1));  // open: reset, Qn, preset
  nor nor_1 (nor_1_out, S1_1, S1_2);
  not not_1 (not_1_out, R1);
  S_R_Flip_Flop #(.trigger("low")) s_r_ff_2 (
    .S(not_2_out), .R(not_3_out), .clk(1'b0), .Q(Q2));  // open: reset, Qn, preset
  not not_2 (not_2_out, S2);
  not not_3 (not_3_out, R2);
  S_R_Flip_Flop #(.trigger("low")) s_r_ff_3 (
    .S(nor_2_out), .R(not_4_out), .clk(1'b0), .Q(Q3));  // open: reset, Qn, preset
  nor nor_2 (nor_2_out, S3_1, S3_2);
  not not_4 (not_4_out, R3);
  S_R_Flip_Flop #(.trigger("low")) s_r_ff_4 (
    .S(not_5_out), .R(not_6_out), .clk(1'b0), .Q(Q4));  // open: reset, Qn, preset
  not not_5 (not_5_out, S4);
  not not_6 (not_6_out, R4);
endmodule

module main (
  input  [7:0] in_1,
  input  [7:0] in_2,
  output [3:0] out_3
);

  wire button_1_out, button_2_out, button_3_out, button_4_out, button_5_out, button_6_out, button_7_out,
       clock_1_out, mem_16x8_1_fin;
  wire [3:0] disp_16x16_1_addrout;
  wire [7:0] mem_16x8_1_dout;
  wire [15:0] disp_16x16_1_col, disp_16x16_1_row, dotmatrix_1_p2, not_1_out;

  // DipSwitch #(.number(1)) dipswitch_1: pin names not known
  Button button_1 (.out(button_1_out));
  Button button_2 (.out(button_2_out));
  Button button_3 (.out(button_3_out));
  mem_16x8 mem_16x8_1 (
    .Din(in_1), .ADDRin(disp_16x16_1_addrout), .WORD(in_2), .CLK(button_1_out), .RUN(button_2_out),
    .HLT(button_3_out), .Dout(mem_16x8_1_dout), .MEM(out_3), .FIN(mem_16x8_1_fin));  // open: WORDen
  Button #(.press("passive")) button_4 (.out(button_4_out));
  Button #(.press("passive")) button_5 (.out(button_5_out));
  Clock clock_1 (.out(clock_1_out));
  Button #(.press("passive")) button_6 (.out(button_6_out));
  Button #(.press("passive")) button_7 (.out(button_7_out));
  disp_16x16 disp_16x16_1 (
    .Xinc(button_4_out), .Xdec(button_5_out), .CLK(clock_1_out), .Din(mem_16x8_1_dout), .Yinc(button_6_out),
    .Ydec(button_7_out), .COL(disp_16x16_1_col), .ADDRout(disp_16x16_1_addrout), .ROW(disp_16x16_1_row));
  assign not_1_out = ~disp_16x16_1_col;  // NOT_Gate not_1, 16 bits wide
  // DotMatrix #(.dotshape("circle"), .inputtype("select"), .matrixcols(16), .matrixrows(16)) dotmatrix_1: pin names not known; wires that end beside it: not_1_out, dotmatrix_1_p2
  assign dotmatrix_1_p2 = mem_16x8_1_fin ? disp_16x16_1_row : 16'bz;  // Controlled_Buffer controlled_buffer_1
endmodule

module mem_64x8 (
);

  SN74LS189 RAM1A ();  // open: nCS, nWE, A3, D4, A2, D3, A1, D2, A0, D1, nO4, nO3, nO2, nO1
  SN74LS189 RAM1B ();  // open: nCS, nWE, A3, D4, A2, D3, A1, D2, A0, D1, nO4, nO3, nO2, nO1
  SN74LS189 RAM2A ();  // open: nCS, nWE, A3, D4, A2, D3, A1, D2, A0, D1, nO4, nO3, nO2, nO1
  SN74LS189 RAM2B ();  // open: nCS, nWE, A3, D4, A2, D3, A1, D2, A0, D1, nO4, nO3, nO2, nO1
  SN74LS189 RAM3A ();  // open: nCS, nWE, A3, D4, A2, D3, A1, D2, A0, D1, nO4, nO3, nO2, nO1
  SN74LS189 RAM3B ();  // open: nCS, nWE, A3, D4, A2, D3, A1, D2, A0, D1, nO4, nO3, nO2, nO1
  SN74LS189 RAM4A ();  // open: nCS, nWE, A3, D4, A2, D3, A1, D2, A0, D1, nO4, nO3, nO2, nO1
  SN74LS189 RAM4B ();  // open: nCS, nWE, A3, D4, A2, D3, A1, D2, A0, D1, nO4, nO3, nO2, nO1
  _74153 u_74153_1 ();  // open: pin1, pin2, pin3, pin4, pin5, pin6, pin7, pin15, pin14, pin13, pin12, pin11, pin10, pin9
  _74153 u_74153_2 ();  // open: pin1, pin2, pin3, pin4, pin5, pin6, pin7, pin15, pin14, pin13, pin12, pin11, pin10, pin9
  _74153 u_74153_3 ();  // open: pin1, pin2, pin3, pin4, pin5, pin6, pin7, pin15, pin14, pin13, pin12, pin11, pin10, pin9
  _74153 u_74153_4 ();  // open: pin1, pin2, pin3, pin4, pin5, pin6, pin7, pin15, pin14, pin13, pin12, pin11, pin10, pin9
endmodule

module disp_16x16 (
  input  Xinc,
  input  Xdec,
  input  CLK,
  input  [7:0] Din,
  input  Yinc,
  input  Ydec,
  output [15:0] COL,
  output [3:0] ADDRout,
  output [15:0] ROW
);

  wire n7404_1_pin1, n7404_1_pin12, n74138_1_pin4, n74138_1_pin5, n74138_2_pin4, n74138_2_pin6,
       n74157_1_pin12, n74157_1_pin14, n74157_1_pin15, n74157_2_pin9, n74157_2_pin10, n74157_2_pin15,
       n74161_1_pin1, n74161_1_pin7, n74161_1_pin9, n74161_1_pin10, n74193_1_pin2, n74193_1_pin3,
       n74193_1_pin6, n74193_1_pin7, n74193_1_pin11, n74283_1_pin3, n74283_1_pin5, n74283_1_pin12,
       n74283_1_pin14, SRQ;

  _74193 u_74193_1 (
    .pin2(n74193_1_pin2), .pin3(n74193_1_pin3), .pin4(Xdec), .pin5(Xinc), .pin6(n74193_1_pin6),
    .pin7(n74193_1_pin7), .pin11(n74193_1_pin11));  // open: pin1, pin15, pin14, pin13, pin12, pin10, pin9
  _74283 u_74283_1 (
    .pin1(ADDRout[1]), .pin2(n74193_1_pin2), .pin3(n74283_1_pin3), .pin4(ADDRout[0]), .pin5(n74283_1_pin5),
    .pin6(n74193_1_pin3), .pin15(n74193_1_pin6), .pin14(n74283_1_pin14), .pin13(ADDRout[2]),
    .pin12(n74283_1_pin12), .pin11(n74193_1_pin7), .pin10(ADDRout[3]));  // open: pin7, pin9
  _74161 u_74161_1 (
    .pin1(n74161_1_pin1), .pin2(CLK), .pin7(n74161_1_pin7), .pin14(n74283_1_pin5), .pin13(n74283_1_pin3),
    .pin12(n74283_1_pin14), .pin11(n74283_1_pin12), .pin10(n74161_1_pin10), .pin9(n74161_1_pin9));  // open: pin3, pin4, pin5, pin6, pin15
  _74157 u_74157_1 (
    .pin1(SRQ), .pin2(Din[5]), .pin3(Din[1]), .pin4(ROW[7]), .pin5(Din[6]), .pin6(Din[2]), .pin7(ROW[9]),
    .pin15(n74157_1_pin15), .pin14(n74157_1_pin14), .pin13(Din[4]), .pin12(n74157_1_pin12), .pin11(Din[7]),
    .pin10(Din[3]), .pin9(ROW[12]));
  SN74LS279 sn74ls279_1 (
    .S1_2(Ydec), .R1(Yinc), .S1_1(Ydec), .Q1(SRQ));  // open: S2, R2, S3_1, S3_2, R3, S4, R4, Q2, Q3, Q4
  _74138 u_74138_1 (
    .pin1(n74283_1_pin5), .pin2(n74283_1_pin3), .pin3(n74283_1_pin14), .pin4(n74138_1_pin4),
    .pin5(n74138_1_pin5), .pin6(n74283_1_pin12), .pin7(COL[15]), .pin15(COL[8]), .pin14(COL[9]),
    .pin13(COL[10]), .pin12(COL[11]), .pin11(COL[12]), .pin10(COL[13]), .pin9(COL[14]));
  _74138 u_74138_2 (
    .pin1(n74283_1_pin5), .pin2(n74283_1_pin3), .pin3(n74283_1_pin14), .pin4(n74138_2_pin4),
    .pin5(n74283_1_pin12), .pin6(n74138_2_pin6), .pin7(COL[7]), .pin15(COL[0]), .pin14(COL[1]),
    .pin13(COL[2]), .pin12(COL[3]), .pin11(COL[4]), .pin10(COL[5]), .pin9(COL[6]));
  _74157 u_74157_2 (
    .pin1(SRQ), .pin2(Din[4]), .pin3(Din[0]), .pin4(ROW[4]), .pin15(n74157_2_pin15), .pin11(Din[3]),
    .pin10(n74157_2_pin10), .pin9(n74157_2_pin9));  // open: pin5, pin6, pin7, pin14, pin13, pin12
  _7404 u_7404_1 (
    .pin1(n7404_1_pin1), .pin2(ROW[1]), .pin13(SRQ), .pin12(n7404_1_pin12));  // open: pin3, pin4, pin5, pin6, pin11, pin10, pin9, pin8
  _7432 u_7432_1 (
    .pin13(n74157_1_pin12), .pin12(n7404_1_pin12), .pin11(ROW[15]));  // open: pin1, pin2, pin3, pin4, pin5, pin6, pin10, pin9, pin8
  _7486 u_7486_1 (
    .pin13(n7404_1_pin12), .pin12(n74157_2_pin9), .pin11(n7404_1_pin1));  // open: pin1, pin2, pin3, pin4, pin5, pin6, pin10, pin9, pin8
  _7404 u_7404_2 (
    .pin1(n74157_2_pin9), .pin2(ROW[0]), .pin3(ROW[4]), .pin4(ROW[3]), .pin5(ROW[7]), .pin6(ROW[6]),
    .pin13(n74157_1_pin12), .pin12(ROW[14]), .pin11(ROW[12]), .pin10(ROW[11]), .pin9(ROW[9]), .pin8(ROW[8]));

  assign {ROW[13], ROW[10], ROW[5], ROW[2]} = 4'b0000;
  // also tied to GND on the sheet: {n74157_1_pin15, n74157_1_pin14, n74138_1_pin4, n74138_2_pin4, n74157_2_pin15, n74138_1_pin5, n74157_2_pin10}
  // also tied to VCC on the sheet: {n74161_1_pin1, n74193_1_pin11, n74161_1_pin10, n74161_1_pin7, n74161_1_pin9, n74138_2_pin6}

  // Other names for the same wires on the sheet: D0 = Din[0]; D3 = Din[3]; D4 = Din[4]; O0 = ROW[1]

  // Notes on the sheet:
  //   Yinc: initial=0x1
  //   Ydec: initial=0x1
endmodule
